# Fritzing sketch Sketch (saved by Fritzing 0.9.9b)
breadboards: 3

parts:
  U1 = ESP32S-HiLetgo [part_number=ESP32S-HiLetgo]
  ESP32_-_Back1 = ESP32 - CAM
  VCC1 = Battery
  5V = RioRand LM2596
  Motor_Driver = DRV8835 Dual Motor Driver Carrier
  M2 = DC Motor
  Shift_Register = 74HC595 SMD [package="SO16 [SMD]"]
  R1 = Resistor [tolerance=±5% power=0.25 resistance=220 package=THT]
  R2 = Resistor [tolerance=±5% power=0.25 resistance=220 package=THT]
  LED1 = LED - 3mm [color="Red (633nm)" current=0.030 package="3 mm [THT]"]
  LED2 = LED - 3mm [color="Red (633nm)" current=0.030 package="3 mm [THT]"]
  LED3 = LED - 3mm [color="Red (633nm)" current=0.030 package="3 mm [THT]"]
  LED4 = LED - 3mm [color="Red (633nm)" current=0.030 package="3 mm [THT]"]
  LED5 = LED - 3mm [color="Red (633nm)" current=0.030 package="3 mm [THT]"]
  LED6 = LED - 3mm [color="Red (633nm)" current=0.030 package="3 mm [THT]"]
  R3 = Resistor [tolerance=±5% power=0.25 resistance=220 package=THT]
  R4 = Resistor [tolerance=±5% power=0.25 resistance=220 package=THT]
  R5 = Resistor [tolerance=±5% power=0.25 resistance=220 package=THT]
  LED7 = LED - 3mm [color="Red (633nm)" current=0.030 package="3 mm [THT]"]
  LED8 = LED - 3mm [color="Red (633nm)" current=0.030 package="3 mm [THT]"]
  R6 = Resistor [tolerance=±5% power=0.25 resistance=220 package=THT]
  R7 = Resistor [tolerance=±5% power=0.25 resistance=220 package=THT]
  R8 = Resistor [tolerance=±5% power=0.25 resistance=220 package=THT]
  Voice_Recognition_Module = elechouse_voice_recognition_module_v3
  R9 = Resistor [tolerance=±5% power=0.25 resistance=220 package=THT]
  R10 = Resistor [tolerance=±5% power=0.25 resistance=220 package=THT]
  R11 = Resistor [tolerance=±5% power=0.25 resistance=220 package=THT]
  LED9 = LED - 3mm [color="Red (633nm)" current=0.030 package="3 mm [THT]"]
  LED10 = LED - 3mm [color="Red (633nm)" current=0.030 package="3 mm [THT]"]
  LED11 = LED - 3mm [color="Red (633nm)" current=0.030 package="3 mm [THT]"]
  LED12 = LED - 3mm [color="Red (633nm)" current=0.030 package="3 mm [THT]"]
  R12 = Resistor [tolerance=±5% power=0.25 resistance=220 package=THT]
  LED13 = LED - 3mm [color="Red (633nm)" current=0.030 package="3 mm [THT]"]
  R13 = Resistor [tolerance=±5% power=0.25 resistance=220 package=THT]
  DFRobot_DFPlayer_Mini1 = DFRobot DFPlayer Mini [part_number=DFR0299]
  부품1 = I2C level shifter bidirectional
  SP1 = SPEAKER [package=pcb_mount_speaker]

nets:
  N1: U1.3.3, 부품1.LV
  N2: U1.GPIO27, DFRobot_DFPlayer_Mini1.TX
  N3: U1.GPIO14, ESP32_-_Back1.GPIO15
  GND: U1.GND, ESP32_-_Back1.GND#7, 5V.Pin_4, Motor_Driver.GND, Motor_Driver.GND-13, Shift_Register.GND, R1.Pin_0, R2.Pin_0, R3.Pin_0, R4.Pin_0, R5.Pin_0, R6.Pin_0, R7.Pin_0, R8.Pin_0, Voice_Recognition_Module.GND, DFRobot_DFPlayer_Mini1.GND-1, DFRobot_DFPlayer_Mini1.GND-2, 부품1.GND
  N4: U1.GPIO13, DFRobot_DFPlayer_Mini1.RX
  VCC: U1.VIN, ESP32_-_Back1.3.3V_/_5V_/_P_OUT, 5V.Pin_3, Motor_Driver.VIN, Shift_Register.MR, Shift_Register.VCC, Voice_Recognition_Module.VCC, DFRobot_DFPlayer_Mini1.VCC, 부품1.HV
  N5: U1.GPIO15, ESP32_-_Back1.GPIO14
  N6: U1.GPIO16, 부품1.LV4
  N7: U1.GPIO17, 부품1.LV3
  N8: U1.GPIO18, Motor_Driver.AIN1/APHASE
  N9: U1.GPIO19, Motor_Driver.AIN2/AENABLE
  N10: U1.GPIO21, Shift_Register.SH_CP
  N11: U1.GPIO22, Shift_Register.ST_CP
  N12: U1.GPIO23, Shift_Register.DS
  N13: ESP32_-_Back1.GPIO4, LED11.anode
  N14: ESP32_-_Back1.GPIO2, LED10.anode
  N15: ESP32_-_Back1.GPIO13, LED9.anode
  N16: ESP32_-_Back1.GPIO12, LED12.anode
  N17: ESP32_-_Back1.GPIO16, LED13.anode
  N18: ESP32_-_Back1.GND#12, ESP32_-_Back1.GND#16, R9.Pin_0, R10.Pin_0, R11.Pin_0, R12.Pin_0, R13.Pin_0
  N19: VCC1.-, 5V.Pin_2
  N20: VCC1.+, 5V.Pin_1
  N21: Motor_Driver.AOUT1, M2.pin_2
  N22: Motor_Driver.AOUT2, M2.pin_1
  N23: Shift_Register.Q1, LED2.anode
  N24: Shift_Register.Q2, LED3.anode
  N25: Shift_Register.Q3, LED4.anode
  N26: Shift_Register.Q4, LED5.anode
  N27: Shift_Register.Q5, LED6.anode
  N28: Shift_Register.Q6, LED7.anode
  N29: Shift_Register.Q7, LED8.anode
  N30: Shift_Register.Q0, LED1.anode
  N31: R1.Pin_1, LED1.cathode
  N32: R2.Pin_1, LED2.cathode
  N33: LED3.cathode, R3.Pin_1
  N34: LED4.cathode, R4.Pin_1
  N35: LED5.cathode, R5.Pin_1
  N36: LED6.cathode, R6.Pin_1
  N37: LED7.cathode, R7.Pin_1
  N38: LED8.cathode, R8.Pin_1
  N39: Voice_Recognition_Module.RXD, 부품1.HV3
  N40: Voice_Recognition_Module.TXD, 부품1.HV4
  N41: R9.Pin_1, LED10.cathode
  N42: R10.Pin_1, LED11.cathode
  N43: R11.Pin_1, LED9.cathode
  N44: LED12.cathode, R12.Pin_1
  N45: LED13.cathode, R13.Pin_1
  N46: DFRobot_DFPlayer_Mini1.SPK_1, SP1.-
  N47: DFRobot_DFPlayer_Mini1.SPK_2, SP1.+

notes:
  Convert to 5V

custom parts:
  ESP32S-HiLetgo: HiLetgo ESP-WROOM-32 ESP32 ESP-32S Development Board 2.4GHz Dual-Mode WiFi + Bluetooth Dual Cores Microcontroller The ESP32 integrated with Antenna switches, RF Balun, power amplifiers, low-noise amplifiers, filters, and management modules, and the entire solution occupies the least area of PCB. 2.4 GHz Wi-Fi plus Bluetooth dual-mode chip, with TSMC Ultra-low power consumption 40nm technology,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
  ESP32 - CAM: The ESP32-CAM has a very competitive small-size camera module that can operate independently as a minimum system with a footprint of only 27*40.5*4.5mm and a deep sleep current of up to 6mA.
  elechouse_voice_recognition_module_v3: Elechouse voice recognition module v3. Module that accepts up to 7 voice commands via a microphone. Note: currently this part was made from a .png image of the board. Thus the pcb is probably not correctly dimensioned since the input data was not precise. Before making boards based on this part, print out the footprint and check it (and provide corrections via the Fritzing forums to correct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
